// Logisim project 16_Bit_processor.circ as structural Verilog: 5 circuits, main circuit Register
module main (
  input  [15:0] PC_in,
  input  in_2,
  output out_3,
  output out_4,
  output out_5,
  output out_6,
  output out_7,
  output out_8,
  output out_9,
  output out_10,
  output [3:0] RX,
  output [15:0] PC_OUT,
  output [31:0] Result,
  output [19:0] IR
);

  wire clock_1_out, MUX_2_out, MUX_out, not_1_out, PC_Shift_out, R_W_prime_shift_out, shift_register_1_out;
  wire [3:0] multiplexer_1_out;
  wire [7:0] multiplexer_2_out, ram_1_data, RB_q, RB_q_2;
  wire [15:0] MAR_q, RA_q, register_1_dataout_16bits, RY_q, RZ_q;
  wire [19:0] rom_1_data;

  PC pc_1 (.PC_in(PC_in), .clock(clock_1_out), .PC_Enable(PC_Shift_out), .PC_out(PC_OUT));
  Clock clock_1 (.out(clock_1_out));
  Shift_Register #(.length(6)) R_W_prime_shift (
    .shift(1'b1), .in(R_W_prime_shift_out), .clk(clock_1_out), .out(R_W_prime_shift_out));  // open: load, clr, d0, q0, d1, q1, d2, q2, d3, q3, d4, q4, d5, q5
  Register_part #(.width(16)) MAR (.D(PC_OUT), .en(PC_Shift_out), .Q(MAR_q), .clk(clock_1_out));  // open: clr
  Shift_Register #(.length(6)) PC_Shift (
    .shift(1'b1), .in(PC_Shift_out), .clk(clock_1_out), .out(PC_Shift_out));  // open: load, clr, d0, q0, d1, q1, d2, q2, d3, q3, d4, q4, d5, q5
  Shift_Register #(.length(6)) MUX (
    .shift(1'b1), .in(MUX_out), .clk(clock_1_out), .out(MUX_out));  // open: load, clr, d0, q0, d1, q1, d2, q2, d3, q3, d4, q4, d5, q5
  ROM #(.addrWidth(16), .dataWidth(20)) rom_1 (.addr(MAR_q), .data(rom_1_data));  // open: sel
  Register_part #(.width(20)) MBR (.D(rom_1_data), .Q(IR), .clk(clock_1_out));  // open: en, clr
  not not_1 (not_1_out, R_W_prime_shift_out);
  Shift_Register #(.length(3)) MUX_2 (
    .shift(1'b1), .in(MUX_2_out), .clk(clock_1_out), .out(MUX_2_out));  // open: load, clr, d0, q0, d1, q1, d2, q2
  Multiplexer #(.width(4), .enable("false")) multiplexer_1 (
    .in0(IR[11:8]), .in1(IR[15:12]), .out(multiplexer_1_out), .sel(MUX_out));
  Register register_1 (
    .in_1(RZ_q), .in_2(multiplexer_1_out), .R_W_prime(R_W_prime_shift_out), .CLOCK(clock_1_out),
    .DataOut_16bits(register_1_dataout_16bits));
  Multiplexer #(.width(8), .enable("false")) multiplexer_2 (
    .in0(IR[7:0]), .in1(RY_q[7:0]), .out(multiplexer_2_out), .sel(MUX_2_out));
  Register_part #(.width(16)) RA (.D(register_1_dataout_16bits), .Q(RA_q), .clk(clock_1_out));  // open: en, clr
  Shift_Register #(.length(3)) shift_register_1 (
    .shift(1'b1), .in(shift_register_1_out), .clk(clock_1_out), .out(shift_register_1_out));  // open: load, clr, d0, q0, d1, q1, d2, q2
  Register_part #(.width(16)) RZ (.D(Result[15:0]), .Q(RZ_q), .clk(clock_1_out));  // open: en, clr
  ALUNEW alunew_1 (
    .A(RA_q), .B({RB_q_2, RB_q}), .in_3(in_2), .OPERATION(IR[19:16]), .RESULT(Result), .out_6(out_6),
    .out_7(out_7), .out_8(out_4), .out_9(out_5), .out_10(out_3), .out_11(out_8), .out_12(out_9),
    .out_13(out_10));
  Hex_Digit_Display hex_digit_display_1 (.value(Result[15:12]));  // open: dp
  RAM #(.bus("separate")) ram_1 (
    .addr(multiplexer_2_out), .din(RB_q), .data(ram_1_data), .str(not_1_out), .clk(clock_1_out),
    .ld(R_W_prime_shift_out));  // open: sel, clr
  Hex_Digit_Display hex_digit_display_2 (.value(Result[11:8]));  // open: dp
  Register_part RY (.D(ram_1_data), .Q(RY_q[7:0]), .clk(clock_1_out));  // open: en, clr
  assign RY_q[15:8] = {{7{1'b0}}, 1'b0};  // Bit_Extender bit_extender_1
  Hex_Digit_Display hex_digit_display_3 (.value(Result[3:0]));  // open: dp
  Hex_Digit_Display hex_digit_display_4 (.value(Result[7:4]));  // open: dp
  Register_part #(.width(16)) RB (
    .D(RY_q), .en(shift_register_1_out), .Q({RB_q_2, RB_q}), .clk(clock_1_out));  // open: clr

  assign RX = IR[11:8];

  // Other names for the same wires on the sheet: Carry = out_6; Even_parity = out_9; Half_carry = out_7;
  //   Negative = out_5; Odd_parity = out_8; Overflow_flag = out_10; Positive = out_4; Zero_flag = out_3

  // Notes on the sheet:
  //   011111
  //   Core mem
  //   00001
  //   contents of rom_1 (hex, n*v repeats v):
  //   51401 25101 0 0 9001
  //   100
  //   001
  //   Data memory
  //   RESULT
endmodule

module Register (
  input  [15:0] in_1,
  input  [3:0] in_2,
  input  R_W_prime,
  input  CLOCK,
  output [15:0] DataOut_16bits
);

  wire decoder_1_out0, decoder_1_out1, decoder_1_out2, decoder_1_out3, decoder_1_out4, decoder_1_out5,
       decoder_1_out6, decoder_1_out7, decoder_1_out8, decoder_1_out9, decoder_1_out10, decoder_1_out11,
       decoder_1_out12, decoder_1_out13, decoder_1_out14, decoder_1_out15, not_1_out;
  wire [15:0] R0_q, R1_q, R2_q, R3_q, R4_q, R5_q, R6_q, R7_q, R8_q, R9_q, R10_q, R11_q, R12_q, R13_q, R14_q,
       R15_q;

  Decoder #(.select(4), .disabled(0)) decoder_1 (
    .out0(decoder_1_out0), .out1(decoder_1_out1), .out2(decoder_1_out2), .out3(decoder_1_out3),
    .out4(decoder_1_out4), .out5(decoder_1_out5), .out6(decoder_1_out6), .out7(decoder_1_out7),
    .out8(decoder_1_out8), .out9(decoder_1_out9), .out10(decoder_1_out10), .out11(decoder_1_out11),
    .out12(decoder_1_out12), .out13(decoder_1_out13), .out14(decoder_1_out14), .out15(decoder_1_out15),
    .sel(in_2), .en(not_1_out));
  not not_1 (not_1_out, R_W_prime);
  Register_part #(.width(16)) R0 (.D(in_1), .en(decoder_1_out0), .Q(R0_q), .clk(CLOCK));  // open: clr
  Register_part #(.width(16)) R1 (.D(in_1), .en(decoder_1_out1), .Q(R1_q), .clk(CLOCK));  // open: clr
  Register_part #(.width(16)) R2 (.D(in_1), .en(decoder_1_out2), .Q(R2_q), .clk(CLOCK));  // open: clr
  Register_part #(.width(16)) R3 (.D(in_1), .en(decoder_1_out3), .Q(R3_q), .clk(CLOCK));  // open: clr
  Register_part #(.width(16)) R4 (.D(in_1), .en(decoder_1_out4), .Q(R4_q), .clk(CLOCK));  // open: clr
  Register_part #(.width(16)) R5 (.D(in_1), .en(decoder_1_out5), .Q(R5_q), .clk(CLOCK));  // open: clr
  Register_part #(.width(16)) R6 (.D(in_1), .en(decoder_1_out6), .Q(R6_q), .clk(CLOCK));  // open: clr
  Register_part #(.width(16)) R7 (.D(in_1), .en(decoder_1_out7), .Q(R7_q), .clk(CLOCK));  // open: clr
  Register_part #(.width(16)) R8 (.D(in_1), .en(decoder_1_out8), .Q(R8_q), .clk(CLOCK));  // open: clr
  Register_part #(.width(16)) R9 (.D(in_1), .en(decoder_1_out9), .Q(R9_q), .clk(CLOCK));  // open: clr
  Register_part #(.width(16)) R10 (.D(in_1), .en(decoder_1_out10), .Q(R10_q), .clk(CLOCK));  // open: clr
  Register_part #(.width(16)) R11 (.D(in_1), .en(decoder_1_out11), .Q(R11_q), .clk(CLOCK));  // open: clr
  Register_part #(.width(16)) R12 (.D(in_1), .en(decoder_1_out12), .Q(R12_q), .clk(CLOCK));  // open: clr
  Register_part #(.width(16)) R13 (.D(in_1), .en(decoder_1_out13), .Q(R13_q), .clk(CLOCK));  // open: clr
  Register_part #(.width(16)) R14 (.D(in_1), .en(decoder_1_out14), .Q(R14_q), .clk(CLOCK));  // open: clr
  Register_part #(.width(16)) R15 (.D(in_1), .en(decoder_1_out15), .Q(R15_q), .clk(CLOCK));  // open: clr
  Multiplexer #(.select(4), .width(16)) multiplexer_1 (
    .in0(R0_q), .in1(R1_q), .in2(R2_q), .in3(R3_q), .in4(R4_q), .in5(R5_q), .in6(R6_q), .in7(R7_q),
    .in8(R8_q), .in9(R9_q), .in10(R10_q), .in11(R11_q), .in12(R12_q), .in13(R13_q), .in14(R14_q),
    .in15(R15_q), .out(DataOut_16bits), .sel(in_2), .en(R_W_prime));
endmodule

module PC (
  input  [15:0] PC_in,
  input  clock,
  input  PC_Enable,
  output [15:0] PC_out
);

  wire [15:0] adder_1_out;

  Adder #(.width(16)) adder_1 (.a(PC_in), .b(PC_out), .out(adder_1_out), .cin(1'b1));  // open: cout
  Hex_Digit_Display hex_digit_display_1 (.value(PC_out[15:12]));  // open: dp
  Register_part #(.width(16)) register_1 (.D(adder_1_out), .en(PC_Enable), .Q(PC_out), .clk(clock));  // open: clr
  Hex_Digit_Display hex_digit_display_2 (.value(PC_out[7:4]));  // open: dp
  Hex_Digit_Display hex_digit_display_3 (.value(PC_out[11:8]));  // open: dp
  Hex_Digit_Display hex_digit_display_4 (.value(PC_out[3:0]));  // open: dp
endmodule

// ALU
module ALUNEW (
  input  [15:0] A,
  input  [15:0] B,
  input  in_3,
  input  [3:0] OPERATION,
  output [31:0] RESULT,
  output out_6,
  output out_7,
  output out_8,
  output out_9,
  output out_10,
  output out_11,
  output out_12,
  output out_13
);

  wire adder_1_cout, or_2_out, or_3_out, subtractor_1_bout;
  wire [15:0] adder_1_out, adder_2_out, and_1_out, bit_extender_1_out, bit_extender_2_out,
       bit_extender_3_out, bit_extender_4_out, divider_1_out, divider_1_rem, multiplier_1_cout,
       multiplier_1_out, not_1_out, or_1_out, shifter_1_out, shifter_2_out, shifter_3_out, shifter_4_out,
       subtractor_1_out, subtractor_2_out;
  wire [31:0] undriven;

  assign bit_extender_1_out = {{15{1'b0}}, 1'b0};  // Bit_Extender bit_extender_1
  assign bit_extender_2_out = {{15{1'b0}}, 1'b0};  // Bit_Extender bit_extender_2
  Adder #(.width(16)) adder_1 (.a(A), .b(B), .out(adder_1_out), .cout(adder_1_cout));  // open: cin
  Subtractor #(.width(16)) subtractor_1 (.a(A), .b(B), .out(subtractor_1_out), .bout(subtractor_1_bout));  // open: bin
  Multiplier #(.width(16)) multiplier_1 (.a(A), .b(B), .out(multiplier_1_out), .cout(multiplier_1_cout));  // open: cin
  Divider #(.width(16)) divider_1 (.a(A), .b(B), .out(divider_1_out), .rem(divider_1_rem));  // open: upper
  Adder #(.width(16)) adder_2 (.a(A), .b(16'h1), .out(adder_2_out), .cin(1'b1));  // open: cout
  Subtractor #(.width(16)) subtractor_2 (.a(A), .b(16'h1), .out(subtractor_2_out), .bin(1'b1));  // open: bout
  assign or_1_out = A | B;  // OR_Gate or_1, 16 bits wide
  assign not_1_out = ~A;  // NOT_Gate not_1, 16 bits wide
  Shifter #(.width(16), .shift("lr")) shifter_1 (.in(A), .\dist (4'b0001), .out(shifter_1_out));
  Shifter #(.width(16)) shifter_2 (.in(A), .\dist (4'b0001), .out(shifter_2_out));
  Shifter #(.width(16), .shift("rr")) shifter_3 (.in(A), .\dist (4'b0001), .out(shifter_3_out));
  Shifter #(.width(16), .shift("rl")) shifter_4 (.in(A), .\dist (4'b0001), .out(shifter_4_out));
  assign bit_extender_3_out = {{15{1'b0}}, adder_1_cout};  // Bit_Extender bit_extender_3
  assign bit_extender_4_out = {{15{1'b0}}, subtractor_1_bout};  // Bit_Extender bit_extender_4
  assign and_1_out = A & B;  // AND_Gate and_1, 16 bits wide
  Multiplexer #(.enable("false")) multiplexer_1 (.in0(adder_1_cout), .in1(subtractor_1_bout), .out(out_6), .sel(in_3));
  Multiplexer #(.select(4), .width(32), .enable("false")) multiplexer_2 (
    .in0({bit_extender_2_out, B}), .in1({bit_extender_2_out, B}), .in2({bit_extender_3_out, adder_1_out}),
    .in3({bit_extender_4_out, subtractor_1_out}), .in4({multiplier_1_cout, multiplier_1_out}),
    .in5({divider_1_rem, divider_1_out}), .in6({bit_extender_1_out, adder_2_out}),
    .in7({bit_extender_1_out, subtractor_2_out}), .in8({bit_extender_1_out, and_1_out}),
    .in9({bit_extender_1_out, or_1_out}), .in10({bit_extender_1_out, not_1_out}), .in11(undriven),
    .in12({bit_extender_1_out, shifter_1_out}), .in13({bit_extender_1_out, shifter_2_out}),
    .in14({bit_extender_1_out, shifter_3_out}), .in15({bit_extender_1_out, shifter_4_out}),
    .out({RESULT[31:16], out_9, RESULT[14:0]}), .sel(OPERATION));
  or or_2 (or_2_out, RESULT[0], RESULT[1], RESULT[2], RESULT[3], RESULT[4], RESULT[5], RESULT[6], RESULT[7], RESULT[8], RESULT[9], RESULT[10], RESULT[11], RESULT[12], RESULT[13], RESULT[14], out_9, RESULT[16], RESULT[17], RESULT[18], RESULT[19], RESULT[20], RESULT[21], RESULT[22], RESULT[23], RESULT[24], RESULT[25], RESULT[26], RESULT[27], RESULT[28], RESULT[29], RESULT[30], RESULT[31]);
  not not_2 (out_7, or_2_out);
  xor odd_parity_1 (out_11, RESULT[0], RESULT[1], RESULT[2], RESULT[3], RESULT[4], RESULT[5], RESULT[6], RESULT[7], RESULT[8], RESULT[9], RESULT[10], RESULT[11], RESULT[12], RESULT[13], RESULT[14], out_9, RESULT[16], RESULT[17], RESULT[18], RESULT[19], RESULT[20], RESULT[21], RESULT[22], RESULT[23], RESULT[24], RESULT[25], RESULT[26], RESULT[27], RESULT[28], RESULT[29], RESULT[30], RESULT[31]);
  xnor even_parity_1 (out_12, RESULT[0], RESULT[1], RESULT[2], RESULT[3], RESULT[4], RESULT[5], RESULT[6], RESULT[7], RESULT[8], RESULT[9], RESULT[10], RESULT[11], RESULT[12], RESULT[13], RESULT[14], out_9, RESULT[16], RESULT[17], RESULT[18], RESULT[19], RESULT[20], RESULT[21], RESULT[22], RESULT[23], RESULT[24], RESULT[25], RESULT[26], RESULT[27], RESULT[28], RESULT[29], RESULT[30], RESULT[31]);
  and and_2 (out_13, RESULT[0], RESULT[1], RESULT[2], RESULT[3], RESULT[4], RESULT[5], RESULT[6], RESULT[7], RESULT[8], RESULT[9], RESULT[10], RESULT[11], RESULT[12], RESULT[13], RESULT[14], out_9, RESULT[16], RESULT[17], RESULT[18], RESULT[19], RESULT[20], RESULT[21], RESULT[22], RESULT[23], RESULT[24], RESULT[25], RESULT[26], RESULT[27], RESULT[28], RESULT[29], RESULT[30], RESULT[31]);
  not not_3 (out_8, out_9);
  or or_3 (or_3_out, RESULT[0], RESULT[1], RESULT[2], RESULT[3], RESULT[4], RESULT[5], RESULT[6], RESULT[7], RESULT[8], RESULT[9], RESULT[10], RESULT[11], RESULT[12], RESULT[13], RESULT[14], out_9);
  not not_4 (out_10, or_3_out);

  assign RESULT[15] = out_9;

  // Other names for the same wires on the sheet: Carry = out_6; Even_parity = out_12; Half_carry = out_10;
  //   Odd_parity = out_11; Overflow_flag = out_13; Positive = out_8; Negative = out_9; Zero_flag = out_7
endmodule

module Reg_File (
  input  [15:0] in_1,
  input  [3:0] in_2,
  input  R_W_prime,
  input  CLOCK,
  output [15:0] DataOut_16bits
);

  wire decoder_1_out0, decoder_1_out1, decoder_1_out2, decoder_1_out3, decoder_1_out4, decoder_1_out5,
       decoder_1_out6, decoder_1_out7, decoder_1_out8, decoder_1_out9, decoder_1_out10, decoder_1_out11,
       decoder_1_out12, decoder_1_out13, decoder_1_out14, decoder_1_out15, not_1_out;
  wire [15:0] R0_q, R1_q, R2_q, R3_q, R4_q, R5_q, R6_q, R7_q, R8_q, R9_q, R10_q, R11_q, R12_q, R13_q, R14_q,
       R15_q;

  Decoder #(.select(4), .disabled(0)) decoder_1 (
    .out0(decoder_1_out0), .out1(decoder_1_out1), .out2(decoder_1_out2), .out3(decoder_1_out3),
    .out4(decoder_1_out4), .out5(decoder_1_out5), .out6(decoder_1_out6), .out7(decoder_1_out7),
    .out8(decoder_1_out8), .out9(decoder_1_out9), .out10(decoder_1_out10), .out11(decoder_1_out11),
    .out12(decoder_1_out12), .out13(decoder_1_out13), .out14(decoder_1_out14), .out15(decoder_1_out15),
    .sel(in_2), .en(not_1_out));
  not not_1 (not_1_out, R_W_prime);
  Register_part #(.width(16)) R0 (.D(in_1), .en(decoder_1_out0), .Q(R0_q), .clk(CLOCK));  // open: clr
  Register_part #(.width(16)) R1 (.D(in_1), .en(decoder_1_out1), .Q(R1_q), .clk(CLOCK));  // open: clr
  Register_part #(.width(16)) R2 (.D(in_1), .en(decoder_1_out2), .Q(R2_q), .clk(CLOCK));  // open: clr
  Register_part #(.width(16)) R3 (.D(in_1), .en(decoder_1_out3), .Q(R3_q), .clk(CLOCK));  // open: clr
  Register_part #(.width(16)) R4 (.D(in_1), .en(decoder_1_out4), .Q(R4_q), .clk(CLOCK));  // open: clr
  Register_part #(.width(16)) R5 (.D(in_1), .en(decoder_1_out5), .Q(R5_q), .clk(CLOCK));  // open: clr
  Register_part #(.width(16)) R6 (.D(in_1), .en(decoder_1_out6), .Q(R6_q), .clk(CLOCK));  // open: clr
  Register_part #(.width(16)) R7 (.D(in_1), .en(decoder_1_out7), .Q(R7_q), .clk(CLOCK));  // open: clr
  Register_part #(.width(16)) R8 (.D(in_1), .en(decoder_1_out8), .Q(R8_q), .clk(CLOCK));  // open: clr
  Register_part #(.width(16)) R9 (.D(in_1), .en(decoder_1_out9), .Q(R9_q), .clk(CLOCK));  // open: clr
  Register_part #(.width(16)) R10 (.D(in_1), .en(decoder_1_out10), .Q(R10_q), .clk(CLOCK));  // open: clr
  Register_part #(.width(16)) R11 (.D(in_1), .en(decoder_1_out11), .Q(R11_q), .clk(CLOCK));  // open: clr
  Register_part #(.width(16)) R12 (.D(in_1), .en(decoder_1_out12), .Q(R12_q), .clk(CLOCK));  // open: clr
  Register_part #(.width(16)) R13 (.D(in_1), .en(decoder_1_out13), .Q(R13_q), .clk(CLOCK));  // open: clr
  Register_part #(.width(16)) R14 (.D(in_1), .en(decoder_1_out14), .Q(R14_q), .clk(CLOCK));  // open: clr
  Register_part #(.width(16)) R15 (.D(in_1), .en(decoder_1_out15), .Q(R15_q), .clk(CLOCK));  // open: clr
  Multiplexer #(.select(4), .width(16)) multiplexer_1 (
    .in0(R0_q), .in1(R1_q), .in2(R2_q), .in3(R3_q), .in4(R4_q), .in5(R5_q), .in6(R6_q), .in7(R7_q),
    .in8(R8_q), .in9(R9_q), .in10(R10_q), .in11(R11_q), .in12(R12_q), .in13(R13_q), .in14(R14_q),
    .in15(R15_q), .out(DataOut_16bits), .sel(in_2), .en(R_W_prime));
endmodule
